// Logisim project FUNCIONANDO...OK.circ as structural Verilog: 1 circuit, main circuit main
module main (
  input  in_1,
  input  in_2,
  input  [7:0] in_3,
  output [7:0] out_4
);

  wire clock_1_out, clock_2_out, comparator_1_eq, not_1_out;
  wire [6:0] keyboard_1_data;
  wire [7:0] counter_1_q, ram_1_data;

  Keyboard keyboard_1 (.clk(clock_1_out), .clr(in_1), .data(keyboard_1_data));  // open: re, avail
  Clock clock_1 (.out(clock_1_out));
  Clock clock_2 (.out(clock_2_out));
  Counter counter_1 (.Q(counter_1_q), .clk(clock_2_out), .clr(comparator_1_eq));  // open: load, D, count, carry
  Comparator comparator_1 (.a({1'b0, keyboard_1_data}), .b(in_3), .eq(comparator_1_eq));  // open: gt, lt
  RAM ram_1 (.addr(counter_1_q), .data(ram_1_data), .clk(clock_1_out), .ld(in_2), .clr(comparator_1_eq));  // open: sel
  assign ram_1_data = not_1_out ? {1'b0, keyboard_1_data} : 8'bz;  // Controlled_Buffer controlled_buffer_1
  not not_1 (not_1_out, in_2);
  assign out_4 = in_2 ? ram_1_data : 8'bz;  // Controlled_Buffer controlled_buffer_2
endmodule
