// Logisim project Projeto trbalho m2.circ as structural Verilog: 7 circuits, main circuit main
module main (
  input  in_1
);

  wire and_1_out, and_2_out, and_3_out, and_4_out, and_5_out, and_6_out, and_7_out, and_8_out, clock_1_out,
       clock_2_out, clock_3_out, comparador_1_out_99, comparador_1_sc1, comparador_1_sc2, comparador_1_sc2_2,
       comparador_1_sc2_3, comparador_1_sc2_4, comparador_1_sc2_5, comparador_1_sc2_6, comparador_1_sc2_7,
       comparador_1_sc2_8, comparador_1_sc2_9, comparador_1_sc2_10, comparador_1_sc2_11, comparador_1_sc2_12,
       comparador_1_sc2_13, comparador_1_sc2_14, comparador_1_sc2_15, comparador_1_sc2_16,
       comparador_1_sc2_17, comparador_1_sc2_18, comparador_1_sc2_19, comparador_1_sc2_20,
       comparador_1_sc2_21, comparador_1_sc2_22, comparador_1_sc2_23, comparador_1_sc2_24,
       comparador_1_sc2_25, comparador_1_sc2_26, comparador_1_sc2_27, comparador_1_sc2_28,
       comparador_1_sc2_29, comparador_1_sc2_30, comparator_1_eq, comparator_2_eq, controladorled_1_l0,
       controladorled_1_l1, controladorled_1_l2, controladorled_1_l3, controladorled_1_l4,
       controladorled_1_l5, controladorled_1_l6, controladorled_2_l0, controladorled_2_l1,
       controladorled_2_l2, controladorled_2_l3, controladorled_2_l4, controladorled_2_l5,
       controladorled_2_l6, controladorled_3_l0, controladorled_3_l1, controladorled_3_l2,
       controladorled_3_l3, controladorled_3_l4, controladorled_3_l5, controladorled_3_l6,
       controladorled_4_l0, controladorled_4_l1, controladorled_4_l2, controladorled_4_l3,
       controladorled_4_l4, controladorled_4_l5, controladorled_4_l6, controladorled_5_l0,
       controladorled_5_l1, controladorled_5_l2, controladorled_5_l3, controladorled_5_l4,
       controladorled_5_l5, controladorled_5_l6, not_1_out, not_2_out, not_3_out, not_4_out, not_5_out,
       not_6_out, not_7_out, or_1_out, or_2_out, paredes_1_out_2;
  wire [1:0] joystick_1_x, joystick_1_y;
  wire [3:0] n5disp_1_out_2, n5disp_1_out_3, n5disp_1_out_4, n5disp_1_out_5, n5disp_1_out_6;
  wire [4:0] counter_1_q, counter_2_q, not_8_out, random_1_out, random_2_out;
  wire [15:0] counter_3_q;
  wire [31:0] comparador_1_s1, comparador_1_s2, comparador_1_s2_2, comparador_1_s2_3, comparador_1_s2_4,
       comparador_1_s2_5, comparador_1_s2_6, comparador_1_s2_7, comparador_1_s2_8, comparador_1_s2_9,
       comparador_1_s2_10, comparador_1_s2_11, comparador_1_s2_12, comparador_1_s2_13, comparador_1_s2_14,
       comparador_1_s2_15, comparador_1_s2_16, comparador_1_s2_17, comparador_1_s2_18, comparador_1_s2_19,
       comparador_1_s2_20, comparador_1_s2_21, comparador_1_s2_22, comparador_1_s2_23, comparador_1_s2_24,
       comparador_1_s2_25, comparador_1_s2_26, comparador_1_s2_27, comparador_1_s2_28, comparador_1_s2_29,
       comparador_1_s2_30, comparador_1_s2_31, decoder_1_out0, decoder_2_out0, demultiplexer_1_out0,
       demultiplexer_1_out1, demultiplexer_1_out2, demultiplexer_1_out3, demultiplexer_1_out4,
       demultiplexer_1_out5, demultiplexer_1_out6, demultiplexer_1_out7, demultiplexer_1_out8,
       demultiplexer_1_out9, demultiplexer_1_out10, demultiplexer_1_out11, demultiplexer_1_out12,
       demultiplexer_1_out13, demultiplexer_1_out14, demultiplexer_1_out15, demultiplexer_1_out16,
       demultiplexer_1_out17, demultiplexer_1_out18, demultiplexer_1_out19, demultiplexer_1_out20,
       demultiplexer_1_out21, demultiplexer_1_out22, demultiplexer_1_out23, demultiplexer_1_out24,
       demultiplexer_1_out25, demultiplexer_1_out26, demultiplexer_1_out27, demultiplexer_1_out28,
       demultiplexer_1_out29, demultiplexer_1_out30, demultiplexer_1_out31, demultiplexer_2_out0,
       demultiplexer_2_out1, demultiplexer_2_out2, demultiplexer_2_out3, demultiplexer_2_out4,
       demultiplexer_2_out5, demultiplexer_2_out6, demultiplexer_2_out7, demultiplexer_2_out8,
       demultiplexer_2_out9, demultiplexer_2_out10, demultiplexer_2_out11, demultiplexer_2_out12,
       demultiplexer_2_out13, demultiplexer_2_out14, demultiplexer_2_out15, demultiplexer_2_out16,
       demultiplexer_2_out17, demultiplexer_2_out18, demultiplexer_2_out19, demultiplexer_2_out20,
       demultiplexer_2_out21, demultiplexer_2_out22, demultiplexer_2_out23, demultiplexer_2_out24,
       demultiplexer_2_out25, demultiplexer_2_out26, demultiplexer_2_out27, demultiplexer_2_out28,
       demultiplexer_2_out29, demultiplexer_2_out30, demultiplexer_2_out31;

  Clock clock_1 (.out(clock_1_out));
  not not_1 (not_1_out, in_1);
  Clock clock_2 (.out(clock_2_out));
  not not_2 (not_2_out, joystick_1_x[1]);
  not not_3 (not_3_out, joystick_1_x[0]);
  and and_1 (and_1_out, not_3_out, joystick_1_x[1]);
  not not_4 (not_4_out, joystick_1_y[0]);
  and and_2 (and_2_out, not_4_out, joystick_1_y[1]);
  not not_5 (not_5_out, and_2_out);
  and and_3 (and_3_out, clock_2_out, or_2_out);
  and and_4 (and_4_out, joystick_1_x[0], not_2_out);
  not not_6 (not_6_out, and_1_out);
  and and_5 (and_5_out, clock_1_out, not_5_out);
  and and_6 (and_6_out, joystick_1_y[0], not_7_out);
  not not_7 (not_7_out, joystick_1_y[1]);
  Random #(.width(5), .seed(1991), .trigger("falling")) random_1 (
    .clk(and_3_out), .out(random_1_out));  // open: next, clr
  and and_7 (and_7_out, not_6_out, clock_1_out);
  Counter #(.width(5), .max('h1f), .ongoal("stay")) counter_1 (
    .load(and_6_out), .Q(counter_1_q), .clk(and_5_out), .clr(in_1));  // open: D, count, carry
  Counter #(.width(5), .max('h1f), .ongoal("stay")) counter_2 (
    .load(and_4_out), .Q(counter_2_q), .clk(and_7_out), .clr(in_1));  // open: D, count, carry
  assign not_8_out = ~counter_1_q;  // NOT_Gate not_8, 5 bits wide
  Decoder #(.select(5)) decoder_1 (
    .out0(decoder_1_out0[0]), .out1(decoder_1_out0[1]), .out2(decoder_1_out0[2]), .out3(decoder_1_out0[3]),
    .out4(decoder_1_out0[4]), .out5(decoder_1_out0[5]), .out6(decoder_1_out0[6]), .out7(decoder_1_out0[7]),
    .out8(decoder_1_out0[8]), .out9(decoder_1_out0[9]), .out10(decoder_1_out0[10]),
    .out11(decoder_1_out0[11]), .out12(decoder_1_out0[12]), .out13(decoder_1_out0[13]),
    .out14(decoder_1_out0[14]), .out15(decoder_1_out0[15]), .out16(decoder_1_out0[16]),
    .out17(decoder_1_out0[17]), .out18(decoder_1_out0[18]), .out19(decoder_1_out0[19]),
    .out20(decoder_1_out0[20]), .out21(decoder_1_out0[21]), .out22(decoder_1_out0[22]),
    .out23(decoder_1_out0[23]), .out24(decoder_1_out0[24]), .out25(decoder_1_out0[25]),
    .out26(decoder_1_out0[26]), .out27(decoder_1_out0[27]), .out28(decoder_1_out0[28]),
    .out29(decoder_1_out0[29]), .out30(decoder_1_out0[30]), .out31(decoder_1_out0[31]), .sel(not_8_out),
    .en(not_1_out));
  Decoder #(.select(5)) decoder_2 (
    .out0(decoder_2_out0[0]), .out1(decoder_2_out0[1]), .out2(decoder_2_out0[2]), .out3(decoder_2_out0[3]),
    .out4(decoder_2_out0[4]), .out5(decoder_2_out0[5]), .out6(decoder_2_out0[6]), .out7(decoder_2_out0[7]),
    .out8(decoder_2_out0[8]), .out9(decoder_2_out0[9]), .out10(decoder_2_out0[10]),
    .out11(decoder_2_out0[11]), .out12(decoder_2_out0[12]), .out13(decoder_2_out0[13]),
    .out14(decoder_2_out0[14]), .out15(decoder_2_out0[15]), .out16(decoder_2_out0[16]),
    .out17(decoder_2_out0[17]), .out18(decoder_2_out0[18]), .out19(decoder_2_out0[19]),
    .out20(decoder_2_out0[20]), .out21(decoder_2_out0[21]), .out22(decoder_2_out0[22]),
    .out23(decoder_2_out0[23]), .out24(decoder_2_out0[24]), .out25(decoder_2_out0[25]),
    .out26(decoder_2_out0[26]), .out27(decoder_2_out0[27]), .out28(decoder_2_out0[28]),
    .out29(decoder_2_out0[29]), .out30(decoder_2_out0[30]), .out31(decoder_2_out0[31]), .sel(random_1_out),
    .en(not_1_out));
  Clock clock_3 (.out(clock_3_out));
  or or_1 (or_1_out, comparator_1_eq, or_2_out, comparator_2_eq);
  paredes paredes_1 (.in_1(counter_2_q), .out_2(paredes_1_out_2));
  and and_8 (and_8_out, clock_3_out, or_1_out);
  Random #(.width(5), .seed(1504)) random_2 (.clk(and_8_out), .out(random_2_out));  // open: next, clr
  Demultiplexer #(.select(5), .width(32)) demultiplexer_1 (
    .out0(demultiplexer_1_out0), .out1(demultiplexer_1_out1), .out2(demultiplexer_1_out2),
    .out3(demultiplexer_1_out3), .out4(demultiplexer_1_out4), .out5(demultiplexer_1_out5),
    .out6(demultiplexer_1_out6), .out7(demultiplexer_1_out7), .out8(demultiplexer_1_out8),
    .out9(demultiplexer_1_out9), .out10(demultiplexer_1_out10), .out11(demultiplexer_1_out11),
    .out12(demultiplexer_1_out12), .out13(demultiplexer_1_out13), .out14(demultiplexer_1_out14),
    .out15(demultiplexer_1_out15), .out16(demultiplexer_1_out16), .out17(demultiplexer_1_out17),
    .out18(demultiplexer_1_out18), .out19(demultiplexer_1_out19), .out20(demultiplexer_1_out20),
    .out21(demultiplexer_1_out21), .out22(demultiplexer_1_out22), .out23(demultiplexer_1_out23),
    .out24(demultiplexer_1_out24), .out25(demultiplexer_1_out25), .out26(demultiplexer_1_out26),
    .out27(demultiplexer_1_out27), .out28(demultiplexer_1_out28), .out29(demultiplexer_1_out29),
    .out30(demultiplexer_1_out30), .out31(demultiplexer_1_out31), .in(decoder_1_out0), .sel(counter_2_q),
    .en(not_1_out));
  Demultiplexer #(.select(5), .width(32)) demultiplexer_2 (
    .out0(demultiplexer_2_out0), .out1(demultiplexer_2_out1), .out2(demultiplexer_2_out2),
    .out3(demultiplexer_2_out3), .out4(demultiplexer_2_out4), .out5(demultiplexer_2_out5),
    .out6(demultiplexer_2_out6), .out7(demultiplexer_2_out7), .out8(demultiplexer_2_out8),
    .out9(demultiplexer_2_out9), .out10(demultiplexer_2_out10), .out11(demultiplexer_2_out11),
    .out12(demultiplexer_2_out12), .out13(demultiplexer_2_out13), .out14(demultiplexer_2_out14),
    .out15(demultiplexer_2_out15), .out16(demultiplexer_2_out16), .out17(demultiplexer_2_out17),
    .out18(demultiplexer_2_out18), .out19(demultiplexer_2_out19), .out20(demultiplexer_2_out20),
    .out21(demultiplexer_2_out21), .out22(demultiplexer_2_out22), .out23(demultiplexer_2_out23),
    .out24(demultiplexer_2_out24), .out25(demultiplexer_2_out25), .out26(demultiplexer_2_out26),
    .out27(demultiplexer_2_out27), .out28(demultiplexer_2_out28), .out29(demultiplexer_2_out29),
    .out30(demultiplexer_2_out30), .out31(demultiplexer_2_out31), .in(decoder_2_out0), .sel(random_2_out),
    .en(not_1_out));
  Comparator #(.width(5)) comparator_1 (.a({5{1'b1}}), .b(random_2_out), .eq(comparator_1_eq));  // open: gt, lt
  Comparator #(.width(5)) comparator_2 (.a(random_2_out), .b({5{1'b0}}), .eq(comparator_2_eq));  // open: gt, lt
  Joystick #(.bits(2)) joystick_1 (.x(joystick_1_x), .y(joystick_1_y));
  DotMatrix #(.matrixcols(32), .matrixrows(32)) dotmatrix_1 (
    .col0(comparador_1_s1), .col1(comparador_1_s2), .col2(comparador_1_s2_2), .col3(comparador_1_s2_3),
    .col4(comparador_1_s2_4), .col5(comparador_1_s2_5), .col6(comparador_1_s2_6), .col7(comparador_1_s2_7),
    .col8(comparador_1_s2_8), .col9(comparador_1_s2_9), .col10(comparador_1_s2_10),
    .col11(comparador_1_s2_11), .col12(comparador_1_s2_12), .col13(comparador_1_s2_13),
    .col14(comparador_1_s2_14), .col15(comparador_1_s2_15), .col16(comparador_1_s2_16),
    .col17(comparador_1_s2_17), .col18(comparador_1_s2_18), .col19(comparador_1_s2_19),
    .col20(comparador_1_s2_20), .col21(comparador_1_s2_21), .col22(comparador_1_s2_22),
    .col23(comparador_1_s2_23), .col24(comparador_1_s2_24), .col25(comparador_1_s2_25),
    .col26(comparador_1_s2_26), .col27(comparador_1_s2_27), .col28(comparador_1_s2_28),
    .col29(comparador_1_s2_29), .col30(comparador_1_s2_30), .col31(comparador_1_s2_31));
  comparador comparador_1 (
    .in_1(demultiplexer_2_out0), .in_2(demultiplexer_1_out1), .in_3(demultiplexer_2_out1),
    .in_4(demultiplexer_1_out2), .in_5(demultiplexer_2_out2), .in_6(demultiplexer_1_out3),
    .in_7(demultiplexer_2_out3), .in_8(demultiplexer_1_out4), .in_9(demultiplexer_2_out4),
    .in_10(demultiplexer_1_out5), .in_11(demultiplexer_2_out5), .in_12(demultiplexer_1_out6),
    .in_13(demultiplexer_2_out6), .in_14(demultiplexer_1_out7), .in_15(demultiplexer_2_out7),
    .in_16(demultiplexer_1_out8), .in_17(demultiplexer_2_out8), .in_18(demultiplexer_1_out9),
    .in_19(demultiplexer_2_out9), .in_20(demultiplexer_1_out10), .in_21(demultiplexer_2_out10),
    .in_22(demultiplexer_1_out11), .in_23(demultiplexer_2_out11), .in_24(demultiplexer_1_out12),
    .in_25(demultiplexer_2_out12), .in_26(demultiplexer_1_out13), .in_27(demultiplexer_2_out13),
    .in_28(demultiplexer_1_out14), .in_29(demultiplexer_2_out14), .in_30(demultiplexer_1_out15),
    .in_31(demultiplexer_2_out15), .in_32(demultiplexer_1_out16), .in_33(demultiplexer_2_out16),
    .in_34(demultiplexer_1_out17), .in_35(demultiplexer_2_out17), .in_36(demultiplexer_1_out18),
    .in_37(demultiplexer_2_out18), .in_38(demultiplexer_1_out19), .in_39(demultiplexer_2_out19),
    .in_40(demultiplexer_1_out20), .in_41(demultiplexer_2_out20), .in_42(demultiplexer_1_out21),
    .in_43(demultiplexer_2_out21), .in_44(demultiplexer_1_out22), .in_45(demultiplexer_2_out22),
    .in_46(demultiplexer_1_out23), .in_47(demultiplexer_2_out23), .in_48(demultiplexer_1_out24),
    .in_49(demultiplexer_2_out24), .in_50(demultiplexer_1_out25), .in_51(demultiplexer_2_out25),
    .in_52(demultiplexer_1_out26), .in_53(demultiplexer_2_out26), .in_54(demultiplexer_1_out27),
    .in_55(demultiplexer_2_out27), .in_56(demultiplexer_1_out28), .in_57(demultiplexer_2_out28),
    .in_58(demultiplexer_1_out29), .in_59(demultiplexer_2_out29), .in_60(demultiplexer_1_out30),
    .in_61(demultiplexer_2_out30), .in_62(demultiplexer_2_out31), .sc1(comparador_1_sc1),
    .s1(comparador_1_s1), .sc2(comparador_1_sc2), .s2(comparador_1_s2), .sc2_2(comparador_1_sc2_2),
    .s2_2(comparador_1_s2_2), .sc2_3(comparador_1_sc2_3), .s2_3(comparador_1_s2_3),
    .sc2_4(comparador_1_sc2_4), .s2_4(comparador_1_s2_4), .sc2_5(comparador_1_sc2_5),
    .s2_5(comparador_1_s2_5), .sc2_6(comparador_1_sc2_6), .s2_6(comparador_1_s2_6),
    .sc2_7(comparador_1_sc2_7), .s2_7(comparador_1_s2_7), .sc2_8(comparador_1_sc2_8),
    .s2_8(comparador_1_s2_8), .sc2_9(comparador_1_sc2_9), .s2_9(comparador_1_s2_9),
    .sc2_10(comparador_1_sc2_10), .s2_10(comparador_1_s2_10), .sc2_11(comparador_1_sc2_11),
    .s2_11(comparador_1_s2_11), .sc2_12(comparador_1_sc2_12), .s2_12(comparador_1_s2_12),
    .sc2_13(comparador_1_sc2_13), .s2_13(comparador_1_s2_13), .sc2_14(comparador_1_sc2_14),
    .s2_14(comparador_1_s2_14), .sc2_15(comparador_1_sc2_15), .s2_15(comparador_1_s2_15),
    .sc2_16(comparador_1_sc2_16), .s2_16(comparador_1_s2_16), .sc2_17(comparador_1_sc2_17),
    .s2_17(comparador_1_s2_17), .out_99(comparador_1_out_99), .s2_18(comparador_1_s2_18),
    .sc2_18(comparador_1_sc2_18), .s2_19(comparador_1_s2_19), .sc2_19(comparador_1_sc2_19),
    .s2_20(comparador_1_s2_20), .sc2_20(comparador_1_sc2_20), .s2_21(comparador_1_s2_21),
    .sc2_21(comparador_1_sc2_21), .s2_22(comparador_1_s2_22), .sc2_22(comparador_1_sc2_22),
    .s2_23(comparador_1_s2_23), .sc2_23(comparador_1_sc2_23), .s2_24(comparador_1_s2_24),
    .sc2_24(comparador_1_sc2_24), .s2_25(comparador_1_s2_25), .sc2_25(comparador_1_sc2_25),
    .s2_26(comparador_1_s2_26), .sc2_26(comparador_1_sc2_26), .s2_27(comparador_1_s2_27),
    .sc2_27(comparador_1_sc2_27), .s2_28(comparador_1_s2_28), .sc2_28(comparador_1_sc2_28),
    .s2_29(comparador_1_s2_29), .sc2_29(comparador_1_sc2_29), .s2_30(comparador_1_s2_30),
    .sc2_30(comparador_1_sc2_30), .s2_31(comparador_1_s2_31));
  or or_2 (or_2_out, comparador_1_sc2, comparador_1_sc2_2, comparador_1_sc2_3, comparador_1_sc2_4, comparador_1_sc2_5, comparador_1_sc2_6, comparador_1_sc2_7, comparador_1_sc2_8, comparador_1_sc2_9, comparador_1_sc2_10, comparador_1_sc2_11, comparador_1_sc2_12, comparador_1_sc2_13, comparador_1_sc2_14, comparador_1_sc2_15, comparador_1_sc2_16, comparador_1_sc2_17, comparador_1_out_99, comparador_1_sc2_18, comparador_1_sc2_19, comparador_1_sc2_20, comparador_1_sc2_21, comparador_1_sc2_22, comparador_1_sc2_23, comparador_1_sc2_24, comparador_1_sc2_25, comparador_1_sc2_26, comparador_1_sc2_27, comparador_1_sc2_28, comparador_1_sc2_29, comparador_1_sc2_30, comparador_1_sc1);
  Counter #(.width(16), .max('hffff)) counter_3 (
    .Q(counter_3_q), .clk(or_2_out), .clr(paredes_1_out_2));  // open: load, D, count, carry
  _5disp u_5disp_1 (
    .in_1(counter_3_q), .out_2(n5disp_1_out_2), .out_3(n5disp_1_out_3), .out_4(n5disp_1_out_4),
    .out_5(n5disp_1_out_5), .out_6(n5disp_1_out_6));
  controladorLED controladorled_1 (
    .in_1(n5disp_1_out_2), .l0(controladorled_1_l0), .l1(controladorled_1_l1), .l2(controladorled_1_l2),
    .l3(controladorled_1_l3), .l4(controladorled_1_l4), .l5(controladorled_1_l5), .l6(controladorled_1_l6));
  controladorLED controladorled_2 (
    .in_1(n5disp_1_out_3), .l0(controladorled_2_l0), .l1(controladorled_2_l1), .l2(controladorled_2_l2),
    .l3(controladorled_2_l3), .l4(controladorled_2_l4), .l5(controladorled_2_l5), .l6(controladorled_2_l6));
  controladorLED controladorled_3 (
    .in_1(n5disp_1_out_4), .l0(controladorled_3_l0), .l1(controladorled_3_l1), .l2(controladorled_3_l2),
    .l3(controladorled_3_l3), .l4(controladorled_3_l4), .l5(controladorled_3_l5), .l6(controladorled_3_l6));
  controladorLED controladorled_4 (
    .in_1(n5disp_1_out_5), .l0(controladorled_4_l0), .l1(controladorled_4_l1), .l2(controladorled_4_l2),
    .l3(controladorled_4_l3), .l4(controladorled_4_l4), .l5(controladorled_4_l5), .l6(controladorled_4_l6));
  controladorLED controladorled_5 (
    .in_1(n5disp_1_out_6), .l0(controladorled_5_l0), .l1(controladorled_5_l1), .l2(controladorled_5_l2),
    .l3(controladorled_5_l3), .l4(controladorled_5_l4), .l5(controladorled_5_l5), .l6(controladorled_5_l6));
  _7_Segment_Display u_7_segment_display_1 (
    .g(controladorled_1_l6), .f(controladorled_1_l5), .a(controladorled_1_l0), .b(controladorled_1_l1),
    .e(controladorled_1_l4), .d(controladorled_1_l3), .c(controladorled_1_l2));  // open: dp
  _7_Segment_Display u_7_segment_display_2 (
    .g(controladorled_3_l6), .f(controladorled_3_l5), .a(controladorled_3_l0), .b(controladorled_3_l1),
    .e(controladorled_3_l4), .d(controladorled_3_l3), .c(controladorled_3_l2));  // open: dp
  _7_Segment_Display u_7_segment_display_3 (
    .g(controladorled_2_l6), .f(controladorled_2_l5), .a(controladorled_2_l0), .b(controladorled_2_l1),
    .e(controladorled_2_l4), .d(controladorled_2_l3), .c(controladorled_2_l2));  // open: dp
  _7_Segment_Display u_7_segment_display_4 (
    .g(controladorled_4_l6), .f(controladorled_4_l5), .a(controladorled_4_l0), .b(controladorled_4_l1),
    .e(controladorled_4_l4), .d(controladorled_4_l3), .c(controladorled_4_l2));  // open: dp
  _7_Segment_Display u_7_segment_display_5 (
    .g(controladorled_5_l6), .f(controladorled_5_l5), .a(controladorled_5_l0), .b(controladorled_5_l1),
    .e(controladorled_5_l4), .d(controladorled_5_l3), .c(controladorled_5_l2));  // open: dp
endmodule

module comparador (
  input  [31:0] in_1,
  input  [31:0] in_2,
  input  [31:0] in_3,
  input  [31:0] in_4,
  input  [31:0] in_5,
  input  [31:0] in_6,
  input  [31:0] in_7,
  input  [31:0] in_8,
  input  [31:0] in_9,
  input  [31:0] in_10,
  input  [31:0] in_11,
  input  [31:0] in_12,
  input  [31:0] in_13,
  input  [31:0] in_14,
  input  [31:0] in_15,
  input  [31:0] in_16,
  input  [31:0] in_17,
  input  [31:0] in_18,
  input  [31:0] in_19,
  input  [31:0] in_20,
  input  [31:0] in_21,
  input  [31:0] in_22,
  input  [31:0] in_23,
  input  [31:0] in_24,
  input  [31:0] in_25,
  input  [31:0] in_26,
  input  [31:0] in_27,
  input  [31:0] in_28,
  input  [31:0] in_29,
  input  [31:0] in_30,
  input  [31:0] in_31,
  input  [31:0] in_32,
  input  [31:0] in_33,
  input  [31:0] in_34,
  input  [31:0] in_35,
  input  [31:0] in_36,
  input  [31:0] in_37,
  input  [31:0] in_38,
  input  [31:0] in_39,
  input  [31:0] in_40,
  input  [31:0] in_41,
  input  [31:0] in_42,
  input  [31:0] in_43,
  input  [31:0] in_44,
  input  [31:0] in_45,
  input  [31:0] in_46,
  input  [31:0] in_47,
  input  [31:0] in_48,
  input  [31:0] in_49,
  input  [31:0] in_50,
  input  [31:0] in_51,
  input  [31:0] in_52,
  input  [31:0] in_53,
  input  [31:0] in_54,
  input  [31:0] in_55,
  input  [31:0] in_56,
  input  [31:0] in_57,
  input  [31:0] in_58,
  input  [31:0] in_59,
  input  [31:0] in_60,
  input  [31:0] in_61,
  input  [31:0] in_62,
  output sc1,
  output [31:0] s1,
  output sc2,
  output [31:0] s2,
  output sc2_2,
  output [31:0] s2_2,
  output sc2_3,
  output [31:0] s2_3,
  output sc2_4,
  output [31:0] s2_4,
  output sc2_5,
  output [31:0] s2_5,
  output sc2_6,
  output [31:0] s2_6,
  output sc2_7,
  output [31:0] s2_7,
  output sc2_8,
  output [31:0] s2_8,
  output sc2_9,
  output [31:0] s2_9,
  output sc2_10,
  output [31:0] s2_10,
  output sc2_11,
  output [31:0] s2_11,
  output sc2_12,
  output [31:0] s2_12,
  output sc2_13,
  output [31:0] s2_13,
  output sc2_14,
  output [31:0] s2_14,
  output sc2_15,
  output [31:0] s2_15,
  output sc2_16,
  output [31:0] s2_16,
  output sc2_17,
  output [31:0] s2_17,
  output out_99,
  output [31:0] s2_18,
  output sc2_18,
  output [31:0] s2_19,
  output sc2_19,
  output [31:0] s2_20,
  output sc2_20,
  output [31:0] s2_21,
  output sc2_21,
  output [31:0] s2_22,
  output sc2_22,
  output [31:0] s2_23,
  output sc2_23,
  output [31:0] s2_24,
  output sc2_24,
  output [31:0] s2_25,
  output sc2_25,
  output [31:0] s2_26,
  output sc2_26,
  output [31:0] s2_27,
  output sc2_27,
  output [31:0] s2_28,
  output sc2_28,
  output [31:0] s2_29,
  output sc2_29,
  output [31:0] s2_30,
  output sc2_30,
  output [31:0] s2_31
);

  wire clock_1_out, clock_2_out, clock_3_out, clock_4_out, clock_5_out, clock_6_out, clock_7_out,
       clock_8_out, clock_9_out, clock_10_out, clock_11_out, clock_12_out, clock_13_out, clock_14_out,
       clock_15_out, clock_16_out, clock_17_out, clock_18_out, clock_19_out, clock_20_out, clock_21_out,
       clock_22_out, clock_23_out, clock_24_out, clock_25_out, clock_26_out, clock_27_out, clock_28_out,
       clock_29_out, clock_30_out, clock_31_out, clock_32_out, comparator_1_eq, comparator_2_eq,
       comparator_3_eq, comparator_4_eq, comparator_5_eq, comparator_6_eq, comparator_7_eq, comparator_8_eq,
       comparator_9_eq, comparator_10_eq, comparator_11_eq, comparator_12_eq, comparator_13_eq,
       comparator_14_eq, comparator_15_eq, comparator_16_eq, comparator_17_eq, comparator_18_eq,
       comparator_19_eq, comparator_20_eq, comparator_21_eq, comparator_22_eq, comparator_23_eq,
       comparator_24_eq, comparator_25_eq, comparator_26_eq, comparator_27_eq, comparator_28_eq,
       comparator_29_eq, comparator_30_eq, comparator_31_eq, comparator_32_eq, not_1_out, not_2_out,
       not_3_out, not_4_out, not_5_out, not_6_out, not_7_out, not_8_out, not_9_out, not_10_out, not_11_out,
       not_12_out, not_13_out, not_14_out, not_15_out, not_16_out, not_17_out, not_18_out, not_19_out,
       not_20_out, not_21_out, not_22_out, not_23_out, not_24_out, not_25_out, not_26_out, not_27_out,
       not_28_out, not_29_out, not_30_out, not_31_out, not_32_out, not_33_out, not_34_out, not_35_out,
       not_36_out, not_37_out, not_38_out, not_39_out, not_40_out, not_41_out, not_42_out, not_43_out,
       not_44_out, not_45_out, not_46_out, not_47_out, not_48_out, not_49_out, not_50_out, not_51_out,
       not_52_out, not_53_out, not_54_out, not_55_out, not_56_out, not_57_out, not_58_out, not_59_out,
       not_60_out, not_61_out, not_62_out, not_63_out, not_64_out;
  wire [31:0] and_1_out, and_2_out, and_3_out, and_4_out, and_5_out, and_6_out, and_7_out, and_8_out,
       and_9_out, and_10_out, and_11_out, and_12_out, and_13_out, and_14_out, and_15_out, and_16_out,
       and_17_out, and_18_out, and_19_out, and_20_out, and_21_out, and_22_out, and_23_out, and_24_out,
       and_25_out, and_26_out, and_27_out, and_28_out, and_29_out, and_30_out, and_31_out, and_32_out,
       controlled_buffer_1_out, controlled_buffer_2_out, controlled_buffer_3_out, controlled_buffer_4_out,
       controlled_buffer_5_out, controlled_buffer_6_out, controlled_buffer_7_out, controlled_buffer_8_out,
       controlled_buffer_9_out, controlled_buffer_10_out, controlled_buffer_11_out, controlled_buffer_12_out,
       controlled_buffer_13_out, controlled_buffer_14_out, controlled_buffer_15_out,
       controlled_buffer_16_out, controlled_buffer_17_out, controlled_buffer_18_out,
       controlled_buffer_19_out, controlled_buffer_20_out, controlled_buffer_21_out,
       controlled_buffer_22_out, controlled_buffer_23_out, controlled_buffer_24_out,
       controlled_buffer_25_out, controlled_buffer_26_out, controlled_buffer_27_out,
       controlled_buffer_28_out, controlled_buffer_29_out, controlled_buffer_30_out,
       controlled_buffer_31_out, controlled_buffer_32_out, controlled_buffer_65_out,
       controlled_buffer_66_out, controlled_buffer_67_out, controlled_buffer_68_out,
       controlled_buffer_69_out, controlled_buffer_70_out, controlled_buffer_71_out,
       controlled_buffer_72_out, controlled_buffer_73_out, controlled_buffer_74_out,
       controlled_buffer_75_out, controlled_buffer_76_out, controlled_buffer_77_out,
       controlled_buffer_78_out, controlled_buffer_79_out, controlled_buffer_80_out,
       controlled_buffer_81_out, controlled_buffer_82_out, controlled_buffer_83_out,
       controlled_buffer_84_out, controlled_buffer_85_out, controlled_buffer_86_out,
       controlled_buffer_87_out, controlled_buffer_88_out, controlled_buffer_89_out,
       controlled_buffer_90_out, controlled_buffer_91_out, controlled_buffer_92_out,
       controlled_buffer_93_out, controlled_buffer_94_out, controlled_buffer_95_out,
       controlled_buffer_96_out, n32bits_1_out_2, n32bits_2_out_2, n32bits_3_out_2, n32bits_4_out_2,
       n32bits_5_out_2, n32bits_6_out_2, n32bits_7_out_2, n32bits_8_out_2, n32bits_9_out_2, n32bits_10_out_2,
       n32bits_11_out_2, n32bits_12_out_2, n32bits_13_out_2, n32bits_14_out_2, n32bits_15_out_2,
       n32bits_16_out_2, n32bits_17_out_2, n32bits_18_out_2, n32bits_19_out_2, n32bits_20_out_2,
       n32bits_21_out_2, n32bits_22_out_2, n32bits_23_out_2, n32bits_24_out_2, n32bits_25_out_2,
       n32bits_26_out_2, n32bits_27_out_2, n32bits_28_out_2, n32bits_29_out_2, n32bits_30_out_2,
       n32bits_31_out_2, n32bits_32_out_2;

  distro distro_1 (.in_1(in_6), .in_2(in_7), .out_3(sc2_3));
  distro distro_2 (.in_1(in_8), .in_2(in_9), .out_3(sc2_4));
  distro distro_3 (.in_1(in_10), .in_2(in_11), .out_3(sc2_5));
  distro distro_4 (.in_1(in_12), .in_2(in_13), .out_3(sc2_6));
  distro distro_5 (.in_1(in_14), .in_2(in_15), .out_3(sc2_7));
  distro distro_6 (.in_1(in_16), .in_2(in_17), .out_3(sc2_8));
  distro distro_7 (.in_1(in_18), .in_2(in_19), .out_3(sc2_9));
  distro distro_8 (.in_1(in_20), .in_2(in_21), .out_3(sc2_10));
  distro distro_9 (.in_1(in_22), .in_2(in_23), .out_3(sc2_11));
  distro distro_10 (.in_1(in_24), .in_2(in_25), .out_3(sc2_12));
  distro distro_11 (.in_1(in_26), .in_2(in_27), .out_3(sc2_13));
  distro distro_12 (.in_1(in_28), .in_2(in_29), .out_3(sc2_14));
  distro distro_13 (.in_1(in_30), .in_2(in_31), .out_3(sc2_15));
  distro distro_14 (.in_1(in_32), .in_2(in_33), .out_3(sc2_16));
  distro distro_15 (.in_1(in_34), .in_2(in_35), .out_3(sc2_17));
  distro distro_16 (.in_1(in_36), .in_2(in_37), .out_3(out_99));
  distro distro_17 (.in_1(in_38), .in_2(in_39), .out_3(sc2_18));
  distro distro_18 (.in_1(in_40), .in_2(in_41), .out_3(sc2_19));
  distro distro_19 (.in_1(in_42), .in_2(in_43), .out_3(sc2_20));
  distro distro_20 (.in_1(in_44), .in_2(in_45), .out_3(sc2_21));
  distro distro_21 (.in_1(in_46), .in_2(in_47), .out_3(sc2_22));
  distro distro_22 (.in_1(in_48), .in_2(in_49), .out_3(sc2_23));
  distro distro_23 (.in_1(in_50), .in_2(in_51), .out_3(sc2_24));
  distro distro_24 (.in_1(in_52), .in_2(in_53), .out_3(sc2_25));
  distro distro_25 (.in_1(in_54), .in_2(in_55), .out_3(sc2_26));
  distro distro_26 (.in_1(in_56), .in_2(in_57), .out_3(sc2_27));
  distro distro_27 (.in_1(in_58), .in_2(in_59), .out_3(sc2_28));
  distro distro_28 (.in_1(in_60), .in_2(in_61), .out_3(sc2_29));
  distro distro_29 (.in_1(in_62), .in_2({32{1'b1}}), .out_3(sc2_30));
  distro distro_30 (.in_1(in_1), .in_2({32{1'b1}}), .out_3(sc1));
  distro distro_31 (.in_1(in_2), .in_2(in_3), .out_3(sc2));
  distro distro_32 (.in_1(in_4), .in_2(in_5), .out_3(sc2_2));
  Comparator #(.width(32)) comparator_1 (.a(in_6), .b(in_7), .eq(comparator_1_eq));  // open: gt, lt
  Comparator #(.width(32)) comparator_2 (.a(in_8), .b(in_9), .eq(comparator_2_eq));  // open: gt, lt
  Comparator #(.width(32)) comparator_3 (.a(in_10), .b(in_11), .eq(comparator_3_eq));  // open: gt, lt
  Comparator #(.width(32)) comparator_4 (.a(in_12), .b(in_13), .eq(comparator_4_eq));  // open: gt, lt
  Comparator #(.width(32)) comparator_5 (.a(in_14), .b(in_15), .eq(comparator_5_eq));  // open: gt, lt
  Comparator #(.width(32)) comparator_6 (.a(in_16), .b(in_17), .eq(comparator_6_eq));  // open: gt, lt
  Comparator #(.width(32)) comparator_7 (.a(in_18), .b(in_19), .eq(comparator_7_eq));  // open: gt, lt
  not not_1 (not_1_out, comparator_8_eq);
  Comparator #(.width(32)) comparator_8 (.a(in_20), .b(in_21), .eq(comparator_8_eq));  // open: gt, lt
  not not_2 (not_2_out, comparator_9_eq);
  Comparator #(.width(32)) comparator_9 (.a(in_22), .b(in_23), .eq(comparator_9_eq));  // open: gt, lt
  not not_3 (not_3_out, comparator_10_eq);
  Comparator #(.width(32)) comparator_10 (.a(in_24), .b(in_25), .eq(comparator_10_eq));  // open: gt, lt
  not not_4 (not_4_out, comparator_11_eq);
  Comparator #(.width(32)) comparator_11 (.a(in_26), .b(in_27), .eq(comparator_11_eq));  // open: gt, lt
  not not_5 (not_5_out, comparator_12_eq);
  Comparator #(.width(32)) comparator_12 (.a(in_28), .b(in_29), .eq(comparator_12_eq));  // open: gt, lt
  not not_6 (not_6_out, comparator_13_eq);
  Comparator #(.width(32)) comparator_13 (.a(in_30), .b(in_31), .eq(comparator_13_eq));  // open: gt, lt
  not not_7 (not_7_out, comparator_14_eq);
  Comparator #(.width(32)) comparator_14 (.a(in_32), .b(in_33), .eq(comparator_14_eq));  // open: gt, lt
  not not_8 (not_8_out, comparator_15_eq);
  Comparator #(.width(32)) comparator_15 (.a(in_34), .b(in_35), .eq(comparator_15_eq));  // open: gt, lt
  Comparator #(.width(32)) comparator_16 (.a(in_36), .b(in_37), .eq(comparator_16_eq));  // open: gt, lt
  Comparator #(.width(32)) comparator_17 (.a(in_38), .b(in_39), .eq(comparator_17_eq));  // open: gt, lt
  not not_9 (not_9_out, comparator_18_eq);
  Comparator #(.width(32)) comparator_18 (.a(in_40), .b(in_41), .eq(comparator_18_eq));  // open: gt, lt
  Comparator #(.width(32)) comparator_19 (.a(in_42), .b(in_43), .eq(comparator_19_eq));  // open: gt, lt
  not not_10 (not_10_out, comparator_20_eq);
  Comparator #(.width(32)) comparator_20 (.a(in_44), .b(in_45), .eq(comparator_20_eq));  // open: gt, lt
  not not_11 (not_11_out, comparator_21_eq);
  Comparator #(.width(32)) comparator_21 (.a(in_46), .b(in_47), .eq(comparator_21_eq));  // open: gt, lt
  not not_12 (not_12_out, comparator_22_eq);
  Comparator #(.width(32)) comparator_22 (.a(in_48), .b(in_49), .eq(comparator_22_eq));  // open: gt, lt
  not not_13 (not_13_out, comparator_23_eq);
  Comparator #(.width(32)) comparator_23 (.a(in_50), .b(in_51), .eq(comparator_23_eq));  // open: gt, lt
  not not_14 (not_14_out, comparator_24_eq);
  Comparator #(.width(32)) comparator_24 (.a(in_52), .b(in_53), .eq(comparator_24_eq));  // open: gt, lt
  Comparator #(.width(32)) comparator_25 (.a(in_54), .b(in_55), .eq(comparator_25_eq));  // open: gt, lt
  Comparator #(.width(32)) comparator_26 (.a(in_56), .b(in_57), .eq(comparator_26_eq));  // open: gt, lt
  Comparator #(.width(32)) comparator_27 (.a(in_58), .b(in_59), .eq(comparator_27_eq));  // open: gt, lt
  Comparator #(.width(32)) comparator_28 (.a(in_60), .b(in_61), .eq(comparator_28_eq));  // open: gt, lt
  Comparator #(.width(32)) comparator_29 (.a(in_62), .b({32{1'b1}}), .eq(comparator_29_eq));  // open: gt, lt
  not not_15 (not_15_out, comparator_30_eq);
  Comparator #(.width(32)) comparator_30 (.a(in_1), .b({32{1'b1}}), .eq(comparator_30_eq));  // open: gt, lt
  not not_16 (not_16_out, comparator_30_eq);
  assign controlled_buffer_1_out = not_16_out ? {32{1'b1}} : 32'bz;  // Controlled_Buffer controlled_buffer_1
  not not_17 (not_17_out, comparator_31_eq);
  Comparator #(.width(32)) comparator_31 (.a(in_2), .b(in_3), .eq(comparator_31_eq));  // open: gt, lt
  not not_18 (not_18_out, comparator_31_eq);
  assign controlled_buffer_2_out = not_18_out ? in_3 : 32'bz;  // Controlled_Buffer controlled_buffer_2
  not not_19 (not_19_out, comparator_32_eq);
  Comparator #(.width(32)) comparator_32 (.a(in_4), .b(in_5), .eq(comparator_32_eq));  // open: gt, lt
  not not_20 (not_20_out, comparator_32_eq);
  assign controlled_buffer_3_out = not_20_out ? in_5 : 32'bz;  // Controlled_Buffer controlled_buffer_3
  not not_21 (not_21_out, comparator_1_eq);
  not not_22 (not_22_out, comparator_1_eq);
  assign controlled_buffer_4_out = not_22_out ? in_7 : 32'bz;  // Controlled_Buffer controlled_buffer_4
  not not_23 (not_23_out, comparator_2_eq);
  not not_24 (not_24_out, comparator_2_eq);
  assign controlled_buffer_5_out = not_24_out ? in_9 : 32'bz;  // Controlled_Buffer controlled_buffer_5
  not not_25 (not_25_out, comparator_3_eq);
  not not_26 (not_26_out, comparator_3_eq);
  assign controlled_buffer_6_out = not_26_out ? in_11 : 32'bz;  // Controlled_Buffer controlled_buffer_6
  not not_27 (not_27_out, comparator_4_eq);
  not not_28 (not_28_out, comparator_4_eq);
  assign controlled_buffer_7_out = not_28_out ? in_13 : 32'bz;  // Controlled_Buffer controlled_buffer_7
  not not_29 (not_29_out, comparator_5_eq);
  not not_30 (not_30_out, comparator_5_eq);
  assign controlled_buffer_8_out = not_30_out ? in_15 : 32'bz;  // Controlled_Buffer controlled_buffer_8
  not not_31 (not_31_out, comparator_6_eq);
  not not_32 (not_32_out, comparator_6_eq);
  assign controlled_buffer_9_out = not_32_out ? in_17 : 32'bz;  // Controlled_Buffer controlled_buffer_9
  not not_33 (not_33_out, comparator_7_eq);
  not not_34 (not_34_out, comparator_7_eq);
  assign controlled_buffer_10_out = not_34_out ? in_19 : 32'bz;  // Controlled_Buffer controlled_buffer_10
  not not_35 (not_35_out, comparator_8_eq);
  assign controlled_buffer_11_out = not_35_out ? in_21 : 32'bz;  // Controlled_Buffer controlled_buffer_11
  not not_36 (not_36_out, comparator_9_eq);
  assign controlled_buffer_12_out = not_36_out ? in_23 : 32'bz;  // Controlled_Buffer controlled_buffer_12
  not not_37 (not_37_out, comparator_10_eq);
  assign controlled_buffer_13_out = not_37_out ? in_25 : 32'bz;  // Controlled_Buffer controlled_buffer_13
  not not_38 (not_38_out, comparator_11_eq);
  assign controlled_buffer_14_out = not_38_out ? in_27 : 32'bz;  // Controlled_Buffer controlled_buffer_14
  not not_39 (not_39_out, comparator_12_eq);
  assign controlled_buffer_15_out = not_39_out ? in_29 : 32'bz;  // Controlled_Buffer controlled_buffer_15
  not not_40 (not_40_out, comparator_13_eq);
  assign controlled_buffer_16_out = not_40_out ? in_31 : 32'bz;  // Controlled_Buffer controlled_buffer_16
  not not_41 (not_41_out, comparator_14_eq);
  assign controlled_buffer_17_out = not_41_out ? in_33 : 32'bz;  // Controlled_Buffer controlled_buffer_17
  not not_42 (not_42_out, comparator_15_eq);
  assign controlled_buffer_18_out = not_42_out ? in_35 : 32'bz;  // Controlled_Buffer controlled_buffer_18
  not not_43 (not_43_out, comparator_16_eq);
  not not_44 (not_44_out, comparator_16_eq);
  assign controlled_buffer_19_out = not_44_out ? in_37 : 32'bz;  // Controlled_Buffer controlled_buffer_19
  not not_45 (not_45_out, comparator_17_eq);
  not not_46 (not_46_out, comparator_17_eq);
  assign controlled_buffer_20_out = not_46_out ? in_39 : 32'bz;  // Controlled_Buffer controlled_buffer_20
  not not_47 (not_47_out, comparator_18_eq);
  assign controlled_buffer_21_out = not_47_out ? in_41 : 32'bz;  // Controlled_Buffer controlled_buffer_21
  not not_48 (not_48_out, comparator_19_eq);
  not not_49 (not_49_out, comparator_19_eq);
  assign controlled_buffer_22_out = not_49_out ? in_43 : 32'bz;  // Controlled_Buffer controlled_buffer_22
  not not_50 (not_50_out, comparator_20_eq);
  assign controlled_buffer_23_out = not_50_out ? in_45 : 32'bz;  // Controlled_Buffer controlled_buffer_23
  not not_51 (not_51_out, comparator_21_eq);
  assign controlled_buffer_24_out = not_51_out ? in_47 : 32'bz;  // Controlled_Buffer controlled_buffer_24
  not not_52 (not_52_out, comparator_22_eq);
  assign controlled_buffer_25_out = not_52_out ? in_49 : 32'bz;  // Controlled_Buffer controlled_buffer_25
  not not_53 (not_53_out, comparator_23_eq);
  assign controlled_buffer_26_out = not_53_out ? in_51 : 32'bz;  // Controlled_Buffer controlled_buffer_26
  not not_54 (not_54_out, comparator_24_eq);
  assign controlled_buffer_27_out = not_54_out ? in_53 : 32'bz;  // Controlled_Buffer controlled_buffer_27
  not not_55 (not_55_out, comparator_25_eq);
  not not_56 (not_56_out, comparator_25_eq);
  assign controlled_buffer_28_out = not_56_out ? in_55 : 32'bz;  // Controlled_Buffer controlled_buffer_28
  not not_57 (not_57_out, comparator_26_eq);
  not not_58 (not_58_out, comparator_26_eq);
  assign controlled_buffer_29_out = not_58_out ? in_57 : 32'bz;  // Controlled_Buffer controlled_buffer_29
  not not_59 (not_59_out, comparator_27_eq);
  not not_60 (not_60_out, comparator_27_eq);
  assign controlled_buffer_30_out = not_60_out ? in_59 : 32'bz;  // Controlled_Buffer controlled_buffer_30
  not not_61 (not_61_out, comparator_28_eq);
  not not_62 (not_62_out, comparator_28_eq);
  assign controlled_buffer_31_out = not_62_out ? in_61 : 32'bz;  // Controlled_Buffer controlled_buffer_31
  not not_63 (not_63_out, comparator_29_eq);
  not not_64 (not_64_out, comparator_29_eq);
  assign controlled_buffer_32_out = not_64_out ? {32{1'b1}} : 32'bz;  // Controlled_Buffer controlled_buffer_32
  assign s2_7 = comparator_5_eq ? in_14 : 32'bz;  // Controlled_Buffer controlled_buffer_33
  assign s2_8 = comparator_6_eq ? in_16 : 32'bz;  // Controlled_Buffer controlled_buffer_34
  assign s2_9 = comparator_7_eq ? in_18 : 32'bz;  // Controlled_Buffer controlled_buffer_35
  assign s2_10 = comparator_8_eq ? in_20 : 32'bz;  // Controlled_Buffer controlled_buffer_36
  assign s2_11 = comparator_9_eq ? in_22 : 32'bz;  // Controlled_Buffer controlled_buffer_37
  assign s2_12 = comparator_10_eq ? in_24 : 32'bz;  // Controlled_Buffer controlled_buffer_38
  assign s2_13 = comparator_11_eq ? in_26 : 32'bz;  // Controlled_Buffer controlled_buffer_39
  assign s2_14 = comparator_12_eq ? in_28 : 32'bz;  // Controlled_Buffer controlled_buffer_40
  assign s2_15 = comparator_13_eq ? in_30 : 32'bz;  // Controlled_Buffer controlled_buffer_41
  assign s2_16 = comparator_14_eq ? in_32 : 32'bz;  // Controlled_Buffer controlled_buffer_42
  assign s2_17 = comparator_15_eq ? in_34 : 32'bz;  // Controlled_Buffer controlled_buffer_43
  Clock clock_1 (.out(clock_1_out));
  assign s2_18 = comparator_16_eq ? in_36 : 32'bz;  // Controlled_Buffer controlled_buffer_44
  assign s2_20 = comparator_18_eq ? in_40 : 32'bz;  // Controlled_Buffer controlled_buffer_45
  Clock clock_2 (.out(clock_2_out));
  assign s2_21 = comparator_19_eq ? in_42 : 32'bz;  // Controlled_Buffer controlled_buffer_46
  assign s2_22 = comparator_20_eq ? in_44 : 32'bz;  // Controlled_Buffer controlled_buffer_47
  assign s2_23 = comparator_21_eq ? in_46 : 32'bz;  // Controlled_Buffer controlled_buffer_48
  Clock clock_3 (.out(clock_3_out));
  assign s2_24 = comparator_22_eq ? in_48 : 32'bz;  // Controlled_Buffer controlled_buffer_49
  assign s2_25 = comparator_23_eq ? in_50 : 32'bz;  // Controlled_Buffer controlled_buffer_50
  assign s2_26 = comparator_24_eq ? in_52 : 32'bz;  // Controlled_Buffer controlled_buffer_51
  assign s2_31 = comparator_29_eq ? in_62 : 32'bz;  // Controlled_Buffer controlled_buffer_52
  assign s1 = comparator_30_eq ? in_1 : 32'bz;  // Controlled_Buffer controlled_buffer_53
  Clock clock_4 (.out(clock_4_out));
  assign s2 = comparator_31_eq ? in_2 : 32'bz;  // Controlled_Buffer controlled_buffer_54
  Clock clock_5 (.out(clock_5_out));
  assign s2_2 = comparator_32_eq ? in_4 : 32'bz;  // Controlled_Buffer controlled_buffer_55
  Clock clock_6 (.out(clock_6_out));
  assign s2_3 = comparator_1_eq ? in_6 : 32'bz;  // Controlled_Buffer controlled_buffer_56
  Clock clock_7 (.out(clock_7_out));
  assign s2_4 = comparator_2_eq ? in_8 : 32'bz;  // Controlled_Buffer controlled_buffer_57
  Clock clock_8 (.out(clock_8_out));
  assign s2_5 = comparator_3_eq ? in_10 : 32'bz;  // Controlled_Buffer controlled_buffer_58
  Clock clock_9 (.out(clock_9_out));
  assign s2_6 = comparator_4_eq ? in_12 : 32'bz;  // Controlled_Buffer controlled_buffer_59
  Clock clock_10 (.out(clock_10_out));
  Clock clock_11 (.out(clock_11_out));
  Clock clock_12 (.out(clock_12_out));
  Clock clock_13 (.out(clock_13_out));
  Clock clock_14 (.out(clock_14_out));
  Clock clock_15 (.out(clock_15_out));
  Clock clock_16 (.out(clock_16_out));
  Clock clock_17 (.out(clock_17_out));
  Clock clock_18 (.out(clock_18_out));
  Clock clock_19 (.out(clock_19_out));
  Clock clock_20 (.out(clock_20_out));
  _32bits u_32bits_1 (.in_1(clock_1_out), .out_2(n32bits_1_out_2));
  Clock clock_21 (.out(clock_21_out));
  assign s2_19 = comparator_17_eq ? in_38 : 32'bz;  // Controlled_Buffer controlled_buffer_60
  Clock clock_22 (.out(clock_22_out));
  _32bits u_32bits_2 (.in_1(clock_2_out), .out_2(n32bits_2_out_2));
  Clock clock_23 (.out(clock_23_out));
  Clock clock_24 (.out(clock_24_out));
  _32bits u_32bits_3 (.in_1(clock_3_out), .out_2(n32bits_3_out_2));
  Clock clock_25 (.out(clock_25_out));
  Clock clock_26 (.out(clock_26_out));
  Clock clock_27 (.out(clock_27_out));
  assign s2_27 = comparator_25_eq ? in_54 : 32'bz;  // Controlled_Buffer controlled_buffer_61
  Clock clock_28 (.out(clock_28_out));
  assign s2_28 = comparator_26_eq ? in_56 : 32'bz;  // Controlled_Buffer controlled_buffer_62
  Clock clock_29 (.out(clock_29_out));
  assign s2_29 = comparator_27_eq ? in_58 : 32'bz;  // Controlled_Buffer controlled_buffer_63
  Clock clock_30 (.out(clock_30_out));
  assign s2_30 = comparator_28_eq ? in_60 : 32'bz;  // Controlled_Buffer controlled_buffer_64
  Clock clock_31 (.out(clock_31_out));
  Clock clock_32 (.out(clock_32_out));
  _32bits u_32bits_4 (.in_1(clock_4_out), .out_2(n32bits_4_out_2));
  _32bits u_32bits_5 (.in_1(clock_5_out), .out_2(n32bits_5_out_2));
  _32bits u_32bits_6 (.in_1(clock_6_out), .out_2(n32bits_6_out_2));
  _32bits u_32bits_7 (.in_1(clock_7_out), .out_2(n32bits_7_out_2));
  assign and_1_out = n32bits_7_out_2 & in_6;  // AND_Gate and_1, 32 bits wide
  _32bits u_32bits_8 (.in_1(clock_8_out), .out_2(n32bits_8_out_2));
  assign and_2_out = n32bits_8_out_2 & in_8;  // AND_Gate and_2, 32 bits wide
  _32bits u_32bits_9 (.in_1(clock_9_out), .out_2(n32bits_9_out_2));
  assign and_3_out = n32bits_9_out_2 & in_10;  // AND_Gate and_3, 32 bits wide
  _32bits u_32bits_10 (.in_1(clock_10_out), .out_2(n32bits_10_out_2));
  assign and_4_out = n32bits_10_out_2 & in_12;  // AND_Gate and_4, 32 bits wide
  _32bits u_32bits_11 (.in_1(clock_11_out), .out_2(n32bits_11_out_2));
  assign and_5_out = n32bits_11_out_2 & in_14;  // AND_Gate and_5, 32 bits wide
  _32bits u_32bits_12 (.in_1(clock_12_out), .out_2(n32bits_12_out_2));
  assign and_6_out = n32bits_12_out_2 & in_16;  // AND_Gate and_6, 32 bits wide
  _32bits u_32bits_13 (.in_1(clock_13_out), .out_2(n32bits_13_out_2));
  assign and_7_out = n32bits_13_out_2 & in_18;  // AND_Gate and_7, 32 bits wide
  _32bits u_32bits_14 (.in_1(clock_14_out), .out_2(n32bits_14_out_2));
  assign and_8_out = n32bits_14_out_2 & in_20;  // AND_Gate and_8, 32 bits wide
  _32bits u_32bits_15 (.in_1(clock_15_out), .out_2(n32bits_15_out_2));
  assign and_9_out = n32bits_15_out_2 & in_22;  // AND_Gate and_9, 32 bits wide
  _32bits u_32bits_16 (.in_1(clock_16_out), .out_2(n32bits_16_out_2));
  assign and_10_out = n32bits_16_out_2 & in_24;  // AND_Gate and_10, 32 bits wide
  _32bits u_32bits_17 (.in_1(clock_17_out), .out_2(n32bits_17_out_2));
  assign and_11_out = n32bits_17_out_2 & in_26;  // AND_Gate and_11, 32 bits wide
  _32bits u_32bits_18 (.in_1(clock_18_out), .out_2(n32bits_18_out_2));
  assign and_12_out = n32bits_18_out_2 & in_28;  // AND_Gate and_12, 32 bits wide
  _32bits u_32bits_19 (.in_1(clock_19_out), .out_2(n32bits_19_out_2));
  assign and_13_out = n32bits_19_out_2 & in_30;  // AND_Gate and_13, 32 bits wide
  _32bits u_32bits_20 (.in_1(clock_20_out), .out_2(n32bits_20_out_2));
  assign and_14_out = n32bits_20_out_2 & in_32;  // AND_Gate and_14, 32 bits wide
  assign and_15_out = n32bits_1_out_2 & in_34;  // AND_Gate and_15, 32 bits wide
  _32bits u_32bits_21 (.in_1(clock_21_out), .out_2(n32bits_21_out_2));
  assign and_16_out = n32bits_21_out_2 & in_36;  // AND_Gate and_16, 32 bits wide
  _32bits u_32bits_22 (.in_1(clock_22_out), .out_2(n32bits_22_out_2));
  assign and_17_out = n32bits_22_out_2 & in_38;  // AND_Gate and_17, 32 bits wide
  assign and_18_out = n32bits_2_out_2 & in_40;  // AND_Gate and_18, 32 bits wide
  _32bits u_32bits_23 (.in_1(clock_23_out), .out_2(n32bits_23_out_2));
  assign and_19_out = n32bits_23_out_2 & in_42;  // AND_Gate and_19, 32 bits wide
  _32bits u_32bits_24 (.in_1(clock_24_out), .out_2(n32bits_24_out_2));
  assign and_20_out = n32bits_24_out_2 & in_44;  // AND_Gate and_20, 32 bits wide
  assign and_21_out = n32bits_3_out_2 & in_46;  // AND_Gate and_21, 32 bits wide
  _32bits u_32bits_25 (.in_1(clock_25_out), .out_2(n32bits_25_out_2));
  assign and_22_out = n32bits_25_out_2 & in_48;  // AND_Gate and_22, 32 bits wide
  _32bits u_32bits_26 (.in_1(clock_26_out), .out_2(n32bits_26_out_2));
  assign and_23_out = n32bits_26_out_2 & in_50;  // AND_Gate and_23, 32 bits wide
  _32bits u_32bits_27 (.in_1(clock_27_out), .out_2(n32bits_27_out_2));
  assign and_24_out = n32bits_27_out_2 & in_52;  // AND_Gate and_24, 32 bits wide
  _32bits u_32bits_28 (.in_1(clock_28_out), .out_2(n32bits_28_out_2));
  assign and_25_out = n32bits_28_out_2 & in_54;  // AND_Gate and_25, 32 bits wide
  _32bits u_32bits_29 (.in_1(clock_29_out), .out_2(n32bits_29_out_2));
  assign and_26_out = n32bits_29_out_2 & in_56;  // AND_Gate and_26, 32 bits wide
  _32bits u_32bits_30 (.in_1(clock_30_out), .out_2(n32bits_30_out_2));
  assign and_27_out = n32bits_30_out_2 & in_58;  // AND_Gate and_27, 32 bits wide
  _32bits u_32bits_31 (.in_1(clock_31_out), .out_2(n32bits_31_out_2));
  assign and_28_out = n32bits_31_out_2 & in_60;  // AND_Gate and_28, 32 bits wide
  _32bits u_32bits_32 (.in_1(clock_32_out), .out_2(n32bits_32_out_2));
  assign and_29_out = n32bits_32_out_2 & in_62;  // AND_Gate and_29, 32 bits wide
  assign controlled_buffer_65_out = not_15_out ? and_30_out : 32'bz;  // Controlled_Buffer controlled_buffer_65
  assign and_30_out = n32bits_4_out_2 & in_1;  // AND_Gate and_30, 32 bits wide
  assign controlled_buffer_66_out = not_17_out ? and_31_out : 32'bz;  // Controlled_Buffer controlled_buffer_66
  assign and_31_out = n32bits_5_out_2 & in_2;  // AND_Gate and_31, 32 bits wide
  assign and_32_out = n32bits_6_out_2 & in_4;  // AND_Gate and_32, 32 bits wide
  assign controlled_buffer_67_out = not_19_out ? and_32_out : 32'bz;  // Controlled_Buffer controlled_buffer_67
  assign controlled_buffer_68_out = not_21_out ? and_1_out : 32'bz;  // Controlled_Buffer controlled_buffer_68
  assign controlled_buffer_69_out = not_23_out ? and_2_out : 32'bz;  // Controlled_Buffer controlled_buffer_69
  assign controlled_buffer_70_out = not_25_out ? and_3_out : 32'bz;  // Controlled_Buffer controlled_buffer_70
  assign controlled_buffer_71_out = not_27_out ? and_4_out : 32'bz;  // Controlled_Buffer controlled_buffer_71
  assign controlled_buffer_72_out = not_29_out ? and_5_out : 32'bz;  // Controlled_Buffer controlled_buffer_72
  assign controlled_buffer_73_out = not_31_out ? and_6_out : 32'bz;  // Controlled_Buffer controlled_buffer_73
  assign controlled_buffer_74_out = not_33_out ? and_7_out : 32'bz;  // Controlled_Buffer controlled_buffer_74
  assign controlled_buffer_75_out = not_1_out ? and_8_out : 32'bz;  // Controlled_Buffer controlled_buffer_75
  assign controlled_buffer_76_out = not_2_out ? and_9_out : 32'bz;  // Controlled_Buffer controlled_buffer_76
  assign controlled_buffer_77_out = not_3_out ? and_10_out : 32'bz;  // Controlled_Buffer controlled_buffer_77
  assign controlled_buffer_78_out = not_4_out ? and_11_out : 32'bz;  // Controlled_Buffer controlled_buffer_78
  assign controlled_buffer_79_out = not_5_out ? and_12_out : 32'bz;  // Controlled_Buffer controlled_buffer_79
  assign controlled_buffer_80_out = not_6_out ? and_13_out : 32'bz;  // Controlled_Buffer controlled_buffer_80
  assign controlled_buffer_81_out = not_7_out ? and_14_out : 32'bz;  // Controlled_Buffer controlled_buffer_81
  assign controlled_buffer_82_out = not_8_out ? and_15_out : 32'bz;  // Controlled_Buffer controlled_buffer_82
  assign controlled_buffer_83_out = not_43_out ? and_16_out : 32'bz;  // Controlled_Buffer controlled_buffer_83
  assign controlled_buffer_84_out = not_45_out ? and_17_out : 32'bz;  // Controlled_Buffer controlled_buffer_84
  assign controlled_buffer_85_out = not_9_out ? and_18_out : 32'bz;  // Controlled_Buffer controlled_buffer_85
  assign controlled_buffer_86_out = not_48_out ? and_19_out : 32'bz;  // Controlled_Buffer controlled_buffer_86
  assign controlled_buffer_87_out = not_10_out ? and_20_out : 32'bz;  // Controlled_Buffer controlled_buffer_87
  assign controlled_buffer_88_out = not_11_out ? and_21_out : 32'bz;  // Controlled_Buffer controlled_buffer_88
  assign controlled_buffer_89_out = not_12_out ? and_22_out : 32'bz;  // Controlled_Buffer controlled_buffer_89
  assign controlled_buffer_90_out = not_13_out ? and_23_out : 32'bz;  // Controlled_Buffer controlled_buffer_90
  assign controlled_buffer_91_out = not_14_out ? and_24_out : 32'bz;  // Controlled_Buffer controlled_buffer_91
  assign controlled_buffer_92_out = not_55_out ? and_25_out : 32'bz;  // Controlled_Buffer controlled_buffer_92
  assign controlled_buffer_93_out = not_57_out ? and_26_out : 32'bz;  // Controlled_Buffer controlled_buffer_93
  assign controlled_buffer_94_out = not_59_out ? and_27_out : 32'bz;  // Controlled_Buffer controlled_buffer_94
  assign controlled_buffer_95_out = not_61_out ? and_28_out : 32'bz;  // Controlled_Buffer controlled_buffer_95
  assign controlled_buffer_96_out = not_63_out ? and_29_out : 32'bz;  // Controlled_Buffer controlled_buffer_96
  Adder #(.width(32)) adder_1 (.a(controlled_buffer_66_out), .b(controlled_buffer_2_out), .out(s2));  // open: cin, cout
  Adder #(.width(32)) adder_2 (
    .a(controlled_buffer_67_out), .b(controlled_buffer_3_out), .out(s2_2));  // open: cin, cout
  Adder #(.width(32)) adder_3 (
    .a(controlled_buffer_68_out), .b(controlled_buffer_4_out), .out(s2_3));  // open: cin, cout
  Adder #(.width(32)) adder_4 (
    .a(controlled_buffer_69_out), .b(controlled_buffer_5_out), .out(s2_4));  // open: cin, cout
  Adder #(.width(32)) adder_5 (
    .a(controlled_buffer_70_out), .b(controlled_buffer_6_out), .out(s2_5));  // open: cin, cout
  Adder #(.width(32)) adder_6 (
    .a(controlled_buffer_71_out), .b(controlled_buffer_7_out), .out(s2_6));  // open: cin, cout
  Adder #(.width(32)) adder_7 (
    .a(controlled_buffer_72_out), .b(controlled_buffer_8_out), .out(s2_7));  // open: cin, cout
  Adder #(.width(32)) adder_8 (
    .a(controlled_buffer_73_out), .b(controlled_buffer_9_out), .out(s2_8));  // open: cin, cout
  Adder #(.width(32)) adder_9 (
    .a(controlled_buffer_74_out), .b(controlled_buffer_10_out), .out(s2_9));  // open: cin, cout
  Adder #(.width(32)) adder_10 (
    .a(controlled_buffer_75_out), .b(controlled_buffer_11_out), .out(s2_10));  // open: cin, cout
  Adder #(.width(32)) adder_11 (
    .a(controlled_buffer_76_out), .b(controlled_buffer_12_out), .out(s2_11));  // open: cin, cout
  Adder #(.width(32)) adder_12 (
    .a(controlled_buffer_77_out), .b(controlled_buffer_13_out), .out(s2_12));  // open: cin, cout
  Adder #(.width(32)) adder_13 (
    .a(controlled_buffer_78_out), .b(controlled_buffer_14_out), .out(s2_13));  // open: cin, cout
  Adder #(.width(32)) adder_14 (
    .a(controlled_buffer_79_out), .b(controlled_buffer_15_out), .out(s2_14));  // open: cin, cout
  Adder #(.width(32)) adder_15 (
    .a(controlled_buffer_80_out), .b(controlled_buffer_16_out), .out(s2_15));  // open: cin, cout
  Adder #(.width(32)) adder_16 (
    .a(controlled_buffer_81_out), .b(controlled_buffer_17_out), .out(s2_16));  // open: cin, cout
  Adder #(.width(32)) adder_17 (
    .a(controlled_buffer_82_out), .b(controlled_buffer_18_out), .out(s2_17));  // open: cin, cout
  Adder #(.width(32)) adder_18 (
    .a(controlled_buffer_83_out), .b(controlled_buffer_19_out), .out(s2_18));  // open: cin, cout
  Adder #(.width(32)) adder_19 (
    .a(controlled_buffer_84_out), .b(controlled_buffer_20_out), .out(s2_19));  // open: cin, cout
  Adder #(.width(32)) adder_20 (
    .a(controlled_buffer_85_out), .b(controlled_buffer_21_out), .out(s2_20));  // open: cin, cout
  Adder #(.width(32)) adder_21 (
    .a(controlled_buffer_86_out), .b(controlled_buffer_22_out), .out(s2_21));  // open: cin, cout
  Adder #(.width(32)) adder_22 (
    .a(controlled_buffer_87_out), .b(controlled_buffer_23_out), .out(s2_22));  // open: cin, cout
  Adder #(.width(32)) adder_23 (
    .a(controlled_buffer_88_out), .b(controlled_buffer_24_out), .out(s2_23));  // open: cin, cout
  Adder #(.width(32)) adder_24 (
    .a(controlled_buffer_89_out), .b(controlled_buffer_25_out), .out(s2_24));  // open: cin, cout
  Adder #(.width(32)) adder_25 (
    .a(controlled_buffer_90_out), .b(controlled_buffer_26_out), .out(s2_25));  // open: cin, cout
  Adder #(.width(32)) adder_26 (
    .a(controlled_buffer_91_out), .b(controlled_buffer_27_out), .out(s2_26));  // open: cin, cout
  Adder #(.width(32)) adder_27 (
    .a(controlled_buffer_92_out), .b(controlled_buffer_28_out), .out(s2_27));  // open: cin, cout
  Adder #(.width(32)) adder_28 (
    .a(controlled_buffer_93_out), .b(controlled_buffer_29_out), .out(s2_28));  // open: cin, cout
  Adder #(.width(32)) adder_29 (
    .a(controlled_buffer_94_out), .b(controlled_buffer_30_out), .out(s2_29));  // open: cin, cout
  Adder #(.width(32)) adder_30 (
    .a(controlled_buffer_95_out), .b(controlled_buffer_31_out), .out(s2_30));  // open: cin, cout
  Adder #(.width(32)) adder_31 (
    .a(controlled_buffer_96_out), .b(controlled_buffer_32_out), .out(s2_31));  // open: cin, cout
  Adder #(.width(32)) adder_32 (
    .a(controlled_buffer_65_out), .b(controlled_buffer_1_out), .out(s1));  // open: cin, cout
endmodule

module distro (
  input  [31:0] in_1,
  input  [31:0] in_2,
  output out_3
);

  wire [31:0] and_1_out;

  assign and_1_out = in_1 & in_2;  // AND_Gate and_1, 32 bits wide
  or or_1 (out_3, and_1_out[0], and_1_out[1], and_1_out[2], and_1_out[3], and_1_out[4], and_1_out[5], and_1_out[6], and_1_out[7], and_1_out[8], and_1_out[9], and_1_out[10], and_1_out[11], and_1_out[12], and_1_out[13], and_1_out[14], and_1_out[15], and_1_out[17], and_1_out[18], and_1_out[19], and_1_out[20], and_1_out[21], and_1_out[22], and_1_out[23], and_1_out[24], and_1_out[25], and_1_out[26], and_1_out[27], and_1_out[28], and_1_out[29], and_1_out[30], and_1_out[31], and_1_out[16]);
endmodule

module _5disp (
  input  [15:0] in_1,
  output [3:0] out_2,
  output [3:0] out_3,
  output [3:0] out_4,
  output [3:0] out_5,
  output [3:0] out_6
);

  wire [15:0] divider_1_rem, divider_2_rem, divider_3_rem;
  wire [15:4] divider_1_out, divider_2_out, divider_3_out, divider_4_out, divider_4_rem;

  Divider #(.width(16)) divider_1 (
    .a(in_1), .b(16'h2710), .out({divider_1_out, out_2}), .rem(divider_1_rem));  // open: upper
  Divider #(.width(16)) divider_2 (
    .a(divider_1_rem), .b(16'h3e8), .out({divider_2_out, out_3}), .rem(divider_2_rem));  // open: upper
  Divider #(.width(16)) divider_3 (
    .a(divider_2_rem), .b(16'h64), .out({divider_3_out, out_4}), .rem(divider_3_rem));  // open: upper
  Divider #(.width(16)) divider_4 (
    .a(divider_3_rem), .b(16'ha), .out({divider_4_out, out_5}), .rem({divider_4_rem, out_6}));  // open: upper
endmodule

module controladorLED (
  input  [3:0] in_1,
  output l0,
  output l1,
  output l2,
  output l3,
  output l4,
  output l5,
  output l6
);

  wire and_1_out, and_2_out, and_3_out, and_4_out, and_5_out, and_6_out, and_7_out, and_8_out, and_9_out,
       and_10_out, and_11_out, and_12_out, and_13_out, and_14_out, and_15_out, and_16_out, not_1_out,
       not_2_out, not_3_out, not_4_out, not_5_out, not_6_out, not_7_out, not_8_out, not_9_out, not_10_out,
       not_11_out, not_12_out, not_13_out, not_14_out, not_15_out, not_16_out, not_17_out, not_18_out,
       not_19_out, not_20_out, not_21_out;

  not not_1 (not_1_out, in_1[2]);
  not not_2 (not_2_out, in_1[0]);
  not not_3 (not_3_out, in_1[1]);
  not not_4 (not_4_out, in_1[0]);
  not not_5 (not_5_out, in_1[1]);
  not not_6 (not_6_out, in_1[2]);
  not not_7 (not_7_out, in_1[0]);
  not not_8 (not_8_out, in_1[2]);
  not not_9 (not_9_out, in_1[0]);
  not not_10 (not_10_out, in_1[1]);
  not not_11 (not_11_out, in_1[2]);
  not not_12 (not_12_out, in_1[0]);
  not not_13 (not_13_out, in_1[0]);
  not not_14 (not_14_out, in_1[1]);
  not not_15 (not_15_out, in_1[0]);
  not not_16 (not_16_out, in_1[1]);
  not not_17 (not_17_out, in_1[0]);
  not not_18 (not_18_out, in_1[2]);
  not not_19 (not_19_out, in_1[1]);
  not not_20 (not_20_out, in_1[0]);
  and and_1 (and_1_out, not_1_out, not_2_out);
  and and_2 (and_2_out, in_1[2], in_1[0]);
  not not_21 (not_21_out, in_1[2]);
  and and_3 (and_3_out, not_3_out, not_4_out);
  and and_4 (and_4_out, in_1[1], in_1[0]);
  or or_1 (l2, not_5_out, in_1[0], in_1[2]);
  and and_5 (and_5_out, not_6_out, not_7_out);
  and and_6 (and_6_out, not_8_out, in_1[1]);
  and and_7 (and_7_out, in_1[1], not_9_out);
  and and_8 (and_8_out, in_1[2], not_10_out, in_1[0]);
  and and_9 (and_9_out, not_11_out, not_12_out);
  and and_10 (and_10_out, in_1[1], not_13_out);
  and and_11 (and_11_out, not_14_out, not_15_out);
  and and_12 (and_12_out, in_1[2], not_16_out);
  and and_13 (and_13_out, in_1[2], not_17_out);
  and and_14 (and_14_out, not_18_out, in_1[1]);
  and and_15 (and_15_out, in_1[2], not_19_out);
  and and_16 (and_16_out, in_1[2], not_20_out);
  or or_2 (l0, and_1_out, in_1[1], and_2_out, in_1[3]);
  or or_3 (l1, not_21_out, and_3_out, and_4_out);
  or or_4 (l3, and_5_out, and_6_out, and_7_out, and_8_out, in_1[3]);
  or or_5 (l4, and_9_out, and_10_out);
  or or_6 (l5, and_11_out, and_12_out, and_13_out, in_1[3]);
  or or_7 (l6, and_14_out, and_15_out, and_16_out, in_1[3]);
endmodule

module _32bits (
  input  in_1,
  output [31:0] out_2
);


  assign out_2 = {32{in_1}};
endmodule

module paredes (
  input  [4:0] in_1,
  output out_2
);

  wire comparator_1_eq, comparator_2_eq;

  Comparator #(.width(5)) comparator_1 (.a(in_1), .b({5{1'b1}}), .eq(comparator_1_eq));  // open: gt, lt
  Comparator #(.width(5)) comparator_2 (.a(in_1), .b({5{1'b0}}), .eq(comparator_2_eq));  // open: gt, lt
  or or_1 (out_2, comparator_1_eq, comparator_2_eq);
endmodule
