// Logisim project Trabalho M3.circ as structural Verilog: 5 circuits, main circuit main
module main (
  input  in_1,
  input  mostra_msg_decryptada
);

  wire button_1_out, clear_out, keyboard_1_avail, nodo_1_clr_2, nodo_1_gatilho_crypter,
       nodo_1_gatilho_decrypter, teclado_1_out_2;
  wire [6:0] keyboard_1_data, nodo_1_saida_crypter, nodo_1_saida_decrypter;

  Button button_1 (.out(button_1_out));
  teclado teclado_1 (.in_1(button_1_out), .out_2(teclado_1_out_2));
  Keyboard keyboard_1 (.clk(teclado_1_out_2), .re(1'b1), .clr(in_1), .avail(keyboard_1_avail), .data(keyboard_1_data));
  Button clear (.out(clear_out));
  nodo nodo_1 (
    .entrada_teclado(keyboard_1_data), .clr(clear_out), .gatilho(teclado_1_out_2),
    .available(keyboard_1_avail), .mostrar_msg_decryptada(mostra_msg_decryptada),
    .saida_crypter(nodo_1_saida_crypter), .gatilho_crypter(nodo_1_gatilho_crypter), .clr_2(nodo_1_clr_2),
    .saida_decrypter(nodo_1_saida_decrypter), .gatilho_decrypter(nodo_1_gatilho_decrypter));
  TTY tty_1 (.data(nodo_1_saida_crypter), .clk(nodo_1_gatilho_crypter), .clr(nodo_1_clr_2));  // open: we
  TTY tty_2 (.data(nodo_1_saida_decrypter), .clk(nodo_1_gatilho_decrypter), .clr(nodo_1_clr_2));  // open: we
endmodule

module Cifrador (
  input  \clock_gravaçao ,
  input  [6:0] data,
  input  ld,
  input  in_4,
  output [6:0] leitura
);

  wire comparator_1_eq, not_1_out, not_5_out;
  wire [3:0] counter_1_q, counter_2_q;
  wire [5:1] not_2_out;
  wire [7:0] adder_1_out, controlled_buffer_1_out, ram_1_data;
  wire [7:7] controlled_buffer_4_out;

  Counter #(.width(4), .max('hf)) counter_1 (
    .Q(counter_1_q), .clk(\clock_gravaçao ));  // open: load, D, count, carry, clr
  Adder adder_1 (.a({1'b0, data}), .b(controlled_buffer_1_out), .out(adder_1_out));  // open: cin, cout
  assign controlled_buffer_1_out = comparator_1_eq ? {8{1'b0}} : 8'bz;  // Controlled_Buffer controlled_buffer_1
  assign controlled_buffer_1_out = not_1_out ? {4'b0000, counter_2_q} : 8'bz;  // Controlled_Buffer controlled_buffer_2
  not not_1 (not_1_out, comparator_1_eq);
  Counter #(.width(4), .max('hf)) counter_2 (
    .load(1'b1), .count(1'b1), .Q(counter_2_q), .clk(\clock_gravaçao ));  // open: D, carry, clr
  not not_2 (not_2_out[1], adder_1_out[1]);
  not not_3 (not_2_out[3], adder_1_out[3]);
  not not_4 (not_2_out[5], adder_1_out[5]);
  Comparator comparator_1 (.a({1'b0, data}), .b({8{1'b0}}), .eq(comparator_1_eq));  // open: gt, lt
  RAM #(.addrWidth(4)) ram_1 (
    .addr(counter_1_q), .data(ram_1_data), .clk(\clock_gravaçao ), .ld(ld), .clr(in_4));  // open: sel
  assign ram_1_data = not_5_out ? {adder_1_out[7:6], not_2_out[5], adder_1_out[4], not_2_out[3], adder_1_out[2], not_2_out[1], adder_1_out[0]} : 8'bz;  // Controlled_Buffer controlled_buffer_3
  not not_5 (not_5_out, ld);
  assign {controlled_buffer_4_out[7], leitura} = ld ? ram_1_data : 8'bz;  // Controlled_Buffer controlled_buffer_4
endmodule

module teclado (
  input  in_1,
  output out_2
);

  wire clock_1_out;

  Clock clock_1 (.out(clock_1_out));
  and and_1 (out_2, clock_1_out, in_1);
endmodule

module Decrypter (
  input  \clock_gravaçao ,
  input  [6:0] data,
  input  ld,
  input  clr,
  output [6:0] leitura
);

  wire comparator_1_eq, not_4_out, not_5_out;
  wire [3:0] counter_1_q, counter_2_q;
  wire [5:1] not_1_out;
  wire [7:0] controlled_buffer_1_out, controlled_buffer_3_out, subtractor_1_out;
  wire [7:7] controlled_buffer_4_out;

  Counter #(.width(4), .max('hf)) counter_1 (
    .Q(counter_1_q), .clk(\clock_gravaçao ));  // open: load, D, count, carry, clr
  not not_1 (not_1_out[1], data[1]);
  not not_2 (not_1_out[3], data[3]);
  not not_3 (not_1_out[5], data[5]);
  assign controlled_buffer_1_out = comparator_1_eq ? {8{1'b0}} : 8'bz;  // Controlled_Buffer controlled_buffer_1
  assign controlled_buffer_1_out = not_4_out ? {4'b0000, counter_2_q} : 8'bz;  // Controlled_Buffer controlled_buffer_2
  not not_4 (not_4_out, comparator_1_eq);
  Counter #(.width(4), .max('hf)) counter_2 (
    .load(1'b1), .count(1'b1), .Q(counter_2_q), .clk(\clock_gravaçao ));  // open: D, carry, clr
  Subtractor subtractor_1 (
    .a({1'b0, data[6], not_1_out[5], data[4], not_1_out[3], data[2], not_1_out[1], data[0]}),
    .b(controlled_buffer_1_out), .out(subtractor_1_out));  // open: bin, bout
  Comparator comparator_1 (.a({1'b0, data}), .b({8{1'b0}}), .eq(comparator_1_eq));  // open: gt, lt
  assign controlled_buffer_3_out = not_5_out ? subtractor_1_out : 8'bz;  // Controlled_Buffer controlled_buffer_3
  not not_5 (not_5_out, ld);
  RAM #(.addrWidth(4)) ram_1 (
    .addr(counter_1_q), .data(controlled_buffer_3_out), .clk(\clock_gravaçao ), .ld(ld), .clr(clr));  // open: sel
  assign {controlled_buffer_4_out[7], leitura} = ld ? controlled_buffer_3_out : 8'bz;  // Controlled_Buffer controlled_buffer_4
endmodule

module nodo (
  input  [6:0] entrada_teclado,
  input  clr,
  input  gatilho,
  input  available,
  input  mostrar_msg_decryptada,
  output [6:0] saida_crypter,
  output gatilho_crypter,
  output clr_2,
  output [6:0] saida_decrypter,
  output gatilho_decrypter
);

  wire not_1_out, not_2_out;

  not not_1 (not_1_out, available);
  Cifrador cifrador_1 (
    .\clock_gravaçao (gatilho), .data(entrada_teclado), .ld(not_1_out), .leitura(saida_crypter), .in_4(clr));
  Decrypter decrypter_1 (
    .\clock_gravaçao (gatilho), .data(saida_crypter), .ld(mostrar_msg_decryptada), .leitura(saida_decrypter),
    .clr(clr));
  not not_2 (not_2_out, available);
  and and_1 (gatilho_crypter, not_2_out, gatilho);
  and and_2 (gatilho_decrypter, gatilho, mostrar_msg_decryptada);

  assign clr_2 = clr;
endmodule
